// Logisim project Computador 16 bits.circ as structural Verilog: 17 circuits, main circuit main
module main (
);

  wire and_1_out, comparator_1_eq, D_A, flags_1_am, flags_1_co, flags_1_eq, flags_1_zer, I_O, IO_e, IO_s,
       monitor_1_out_6, monitor_1_out_7, or_1_out, register_1_q, teclado_1_out_8, teclado_1_out_9, uc_1_acce,
       uc_1_accs, uc_1_bus1, uc_1_flags, uc_1_iare, uc_1_iars, uc_1_irs, uc_1_led, uc_1_mars, uc_1_oe,
       uc_1_r0e, uc_1_r0s, uc_1_r1e, uc_1_r1s, uc_1_r2e, uc_1_r2s, uc_1_r3e, uc_1_r3s, uc_1_tmp, uc_1_we,
       ula_1_a_larger, ula_1_equal, ula_1_u_c_out, ula_1_zero;
  wire [2:0] uc_1_ulaop;
  wire [6:0] keyboard_1_data, monitor_1_out_5;
  wire [7:0] ACC_q, bus_1_out_3, controlled_buffer_7_out, IAR_q, IR_q, MAR_q, R0_q, R1_q, R2_q, R3_q,
       teclado_1_stec, TMP_q, ula_1_u_out;

  teclado teclado_1 (
    .ioe(IO_e), .ios(IO_s), .da(D_A), .io(I_O), .ebarr(teclado_1_stec), .stec(teclado_1_stec),
    .etec(keyboard_1_data), .out_8(teclado_1_out_8), .out_9(teclado_1_out_9));
  Register TMP (.D(teclado_1_stec), .Q(TMP_q), .clk(uc_1_tmp));  // open: en, clr
  ULA ula_1 (
    .B(teclado_1_stec), .A(bus_1_out_3), .U_out(ula_1_u_out), .in_1(uc_1_ulaop), .U_c_out(ula_1_u_c_out),
    .a_larger(ula_1_a_larger), .equal(ula_1_equal), .zero(ula_1_zero));
  Keyboard keyboard_1 (.clk(teclado_1_out_8), .re(teclado_1_out_9), .data(keyboard_1_data));  // open: clr, avail
  bus1 bus_1 (.in_1(TMP_q), .out_3(bus_1_out_3), .in_2(uc_1_bus1));
  flags flags_1 (
    .in_1(ula_1_u_c_out), .in_2(ula_1_a_larger), .in_3(ula_1_equal), .in_4(ula_1_zero), .co(flags_1_co),
    .am(flags_1_am), .eq(flags_1_eq), .zer(flags_1_zer), .reset(uc_1_flags));
  Register ACC (.D(ula_1_u_out), .Q(ACC_q), .clk(uc_1_accs));  // open: en, clr
  assign teclado_1_stec = uc_1_acce ? ACC_q : 8'bz;  // Controlled_Buffer controlled_buffer_1
  // Probe on uc_1_ulaop
  Register R0 (.D(teclado_1_stec), .Q(R0_q), .clk(uc_1_r0s));  // open: en, clr
  assign teclado_1_stec = uc_1_r0e ? R0_q : 8'bz;  // Controlled_Buffer controlled_buffer_2
  assign teclado_1_stec = uc_1_r1e ? R1_q : 8'bz;  // Controlled_Buffer controlled_buffer_3
  Register R1 (.D(teclado_1_stec), .Q(R1_q), .clk(uc_1_r1s));  // open: en, clr
  Register IAR (.D(teclado_1_stec), .Q(IAR_q), .clk(uc_1_iars));  // open: en, clr
  monitor monitor_1 (
    .in_1(teclado_1_stec), .ios(IO_s), .da(D_A), .io(I_O), .out_5(monitor_1_out_5), .out_6(monitor_1_out_6),
    .out_7(monitor_1_out_7));
  assign teclado_1_stec = uc_1_r2e ? R2_q : 8'bz;  // Controlled_Buffer controlled_buffer_4
  Register R2 (.D(teclado_1_stec), .Q(R2_q), .clk(uc_1_r2s));  // open: en, clr
  assign teclado_1_stec = uc_1_iare ? IAR_q : 8'bz;  // Controlled_Buffer controlled_buffer_5
  TTY tty_1 (.data(monitor_1_out_5), .clk(monitor_1_out_6), .we(monitor_1_out_7));  // open: clr
  assign teclado_1_stec = uc_1_r3e ? R3_q : 8'bz;  // Controlled_Buffer controlled_buffer_6
  Register R3 (.D(teclado_1_stec), .Q(R3_q), .clk(uc_1_r3s));  // open: en, clr
  Register IR (.D(teclado_1_stec), .Q(IR_q), .clk(uc_1_irs));  // open: en, clr
  uc uc_1 (
    .ULAop(uc_1_ulaop), .c_out(flags_1_co), .alarg(flags_1_am), .equal(flags_1_eq), .zero(flags_1_zer),
    .flags(uc_1_flags), .bus1(uc_1_bus1), .tmp(uc_1_tmp), .r0s(uc_1_r0s), .r0e(uc_1_r0e), .r1s(uc_1_r1s),
    .r1e(uc_1_r1e), .r2s(uc_1_r2s), .r2e(uc_1_r2e), .r3s(uc_1_r3s), .r3e(uc_1_r3e), .mars(uc_1_mars),
    .accs(uc_1_accs), .acce(uc_1_acce), .iars(uc_1_iars), .iare(uc_1_iare), .in_5(IR_q), .irs(uc_1_irs),
    .I_O(I_O), .D_A(D_A), .IO_e(IO_e), .IO_s(IO_s), .we(uc_1_we), .oe(uc_1_oe), .led(uc_1_led));
  LED led_1 (.in(uc_1_led));
  or or_1 (or_1_out, uc_1_we, uc_1_oe);
  // Probe on MAR_q
  Register MAR (.D(teclado_1_stec), .Q(MAR_q), .clk(uc_1_mars));  // open: en, clr
  // Probe on teclado_1_stec
  Comparator comparator_1 (.a(teclado_1_stec), .b(8'h2), .eq(comparator_1_eq));  // open: gt, lt
  and and_1 (and_1_out, IO_s, D_A, I_O);
  RAM #(.databus("bidir"), .\type ("nonvolatile")) ram_1 (
    .addr(MAR_q), .we(uc_1_we), .oe(uc_1_oe), .clk(or_1_out));  // open: data
  Register #(.width(1)) register_1 (.D(comparator_1_eq), .Q(register_1_q), .clk(and_1_out));  // open: en, clr
  assign controlled_buffer_7_out = IO_s ? teclado_1_stec : 8'bz;  // Controlled_Buffer controlled_buffer_7
  // PortIO portio_1: pin names not known; wires that end beside it: register_1_q, controlled_buffer_7_out

  // Notes on the sheet:
  //   Abel Andrade Prazeres dos Santos
  //   Matricula:22450083
  //   7c 71 72 7f
  //   7c 7a 7b 7d 
endmodule

module Somador (
  input  c_in8b,
  input  [7:0] a_8b,
  input  [7:0] b_8b,
  output [7:0] out_8b,
  output c_out8b
);

  wire somador1bit_1_c_out, somador1bit_2_c_out, somador1bit_3_c_out, somador1bit_4_c_out,
       somador1bit_5_c_out, somador1bit_6_c_out, somador1bit_7_c_out;

  somador1bit somador1bit_1 (.a(a_8b[0]), .b(b_8b[0]), .in_1(c_in8b), .C_out(somador1bit_1_c_out), .Sum_out(out_8b[0]));
  somador1bit somador1bit_2 (
    .a(a_8b[1]), .b(b_8b[1]), .in_1(somador1bit_1_c_out), .C_out(somador1bit_2_c_out), .Sum_out(out_8b[1]));
  somador1bit somador1bit_3 (
    .a(a_8b[2]), .b(b_8b[2]), .in_1(somador1bit_2_c_out), .C_out(somador1bit_3_c_out), .Sum_out(out_8b[2]));
  somador1bit somador1bit_4 (
    .a(a_8b[3]), .b(b_8b[3]), .in_1(somador1bit_3_c_out), .C_out(somador1bit_4_c_out), .Sum_out(out_8b[3]));
  somador1bit somador1bit_5 (
    .a(a_8b[4]), .b(b_8b[4]), .in_1(somador1bit_4_c_out), .C_out(somador1bit_5_c_out), .Sum_out(out_8b[4]));
  somador1bit somador1bit_6 (
    .a(a_8b[5]), .b(b_8b[5]), .in_1(somador1bit_5_c_out), .C_out(somador1bit_6_c_out), .Sum_out(out_8b[5]));
  somador1bit somador1bit_7 (
    .a(a_8b[6]), .b(b_8b[6]), .in_1(somador1bit_6_c_out), .C_out(somador1bit_7_c_out), .Sum_out(out_8b[6]));
  somador1bit somador1bit_8 (
    .a(a_8b[7]), .b(b_8b[7]), .in_1(somador1bit_7_c_out), .C_out(c_out8b), .Sum_out(out_8b[7]));
endmodule

module somador1bit (
  input  in_1,
  input  a,
  input  b,
  output Sum_out,
  output C_out
);

  wire and_1_out, and_2_out, and_3_out, xor_1_out;

  xor xor_1 (xor_1_out, a, b);
  and and_1 (and_1_out, in_1, a);
  and and_2 (and_2_out, in_1, b);
  and and_3 (and_3_out, a, b);
  xor xor_2 (Sum_out, xor_1_out, in_1);
  or or_1 (C_out, and_1_out, and_2_out, and_3_out);

  // Notes on the sheet:
  //   c_in
endmodule

module Registrador1bit (
  input  in_1,
  input  in_2,
  output out_3
);

  wire nand_1_out, nand_2_out, nand_4_out;

  nand nand_1 (nand_1_out, in_1, in_2);
  nand nand_2 (nand_2_out, nand_1_out, in_2);
  nand nand_3 (out_3, nand_1_out, nand_4_out);
  nand nand_4 (nand_4_out, out_3, nand_2_out);
endmodule

module Registrador8bits (
  input  [7:0] in_1,
  input  Set,
  input  Enable,
  output [7:0] R_8bits_out
);

  wire registrador1bit_1_out_3, registrador1bit_2_out_3, registrador1bit_3_out_3, registrador1bit_4_out_3,
       registrador1bit_5_out_3, registrador1bit_6_out_3, registrador1bit_7_out_3, registrador1bit_8_out_3;

  Registrador1bit registrador1bit_1 (.in_1(in_1[0]), .in_2(Set), .out_3(registrador1bit_1_out_3));
  Registrador1bit registrador1bit_2 (.in_1(in_1[1]), .in_2(Set), .out_3(registrador1bit_2_out_3));
  Registrador1bit registrador1bit_3 (.in_1(in_1[2]), .in_2(Set), .out_3(registrador1bit_3_out_3));
  Registrador1bit registrador1bit_4 (.in_1(in_1[3]), .in_2(Set), .out_3(registrador1bit_4_out_3));
  Registrador1bit registrador1bit_5 (.in_1(in_1[4]), .in_2(Set), .out_3(registrador1bit_5_out_3));
  Registrador1bit registrador1bit_6 (.in_1(in_1[5]), .in_2(Set), .out_3(registrador1bit_6_out_3));
  Registrador1bit registrador1bit_7 (.in_1(in_1[6]), .in_2(Set), .out_3(registrador1bit_7_out_3));
  Registrador1bit registrador1bit_8 (.in_1(in_1[7]), .in_2(Set), .out_3(registrador1bit_8_out_3));
  assign R_8bits_out[0] = Enable ? registrador1bit_1_out_3 : 1'bz;  // Controlled_Buffer controlled_buffer_1
  assign R_8bits_out[1] = Enable ? registrador1bit_2_out_3 : 1'bz;  // Controlled_Buffer controlled_buffer_2
  assign R_8bits_out[2] = Enable ? registrador1bit_3_out_3 : 1'bz;  // Controlled_Buffer controlled_buffer_3
  assign R_8bits_out[3] = Enable ? registrador1bit_4_out_3 : 1'bz;  // Controlled_Buffer controlled_buffer_4
  assign R_8bits_out[4] = Enable ? registrador1bit_5_out_3 : 1'bz;  // Controlled_Buffer controlled_buffer_5
  assign R_8bits_out[5] = Enable ? registrador1bit_6_out_3 : 1'bz;  // Controlled_Buffer controlled_buffer_6
  assign R_8bits_out[6] = Enable ? registrador1bit_7_out_3 : 1'bz;  // Controlled_Buffer controlled_buffer_7
  assign R_8bits_out[7] = Enable ? registrador1bit_8_out_3 : 1'bz;  // Controlled_Buffer controlled_buffer_8
endmodule

module Decoder2x4 (
  input  in_1,
  input  in_2,
  output out_3,
  output out_4,
  output out_5,
  output out_6
);

  wire not_1_out, not_2_out;

  not not_1 (not_1_out, in_1);
  not not_2 (not_2_out, in_2);
  and and_1 (out_3, not_1_out, not_2_out);
  and and_2 (out_4, not_1_out, in_2);
  and and_3 (out_5, in_1, not_2_out);
  and and_4 (out_6, in_1, in_2);
endmodule

module Memoria256 (
  input  in_1,
  input  in_2,
  input  [7:0] in_3,
  input  [7:0] in_4,
  output [7:0] out_5
);

  wire and_1_out, and_2_out, and_3_out, decoder_1_out0, decoder_2_out0;

  Decoder #(.enable("false"), .select(4)) decoder_1 (
    .out0(decoder_1_out0), .sel(in_3[7:4]));  // open: out1, out2, out3, out4, out5, out6, out7, out8, out9, out10, out11, out12, out13, out14, out15
  Decoder #(.enable("false"), .select(4)) decoder_2 (
    .out0(decoder_2_out0), .sel(in_3[3:0]));  // open: out1, out2, out3, out4, out5, out6, out7, out8, out9, out10, out11, out12, out13, out14, out15
  and and_1 (and_1_out, decoder_2_out0, decoder_1_out0);
  Registrador8bits registrador8bits_1 (.in_1(in_4), .Set(and_2_out), .Enable(and_3_out), .R_8bits_out(out_5));
  and and_2 (and_2_out, and_1_out, in_1);
  and and_3 (and_3_out, and_1_out, in_2);

  // Other names for the same wires on the sheet: oe = in_2; we = in_1
endmodule

module SHR (
  input  [7:0] in_1,
  input  C_outSR,
  output C_inSR,
  output [7:0] out_4
);


  assign C_inSR = in_1[0];
  assign out_4 = {C_outSR, in_1[7:1]};
endmodule

module SHL (
  input  c_inSL,
  input  [7:0] in_2,
  output [7:0] out_3,
  output C_outSL
);


  assign C_outSL = in_2[7];
  assign out_3 = {in_2[6:0], c_inSL};
endmodule

module ULA (
  input  [2:0] in_1,
  input  [7:0] B,
  input  [7:0] A,
  output [7:0] U_out,
  output U_c_out,
  output a_larger,
  output equal,
  output zero
);

  wire SL_c_outsl, somador_1_c_out8b, SR_c_insr;
  wire [7:0] and_1_out, not_1_out, or_1_out, SL_out_3, somador_1_out_8b, SR_out_4, xor_1_out;

  Somador somador_1 (.a_8b(B), .b_8b(A), .c_in8b(1'b0), .c_out8b(somador_1_c_out8b), .out_8b(somador_1_out_8b));
  SHR SR (.in_1(B), .C_inSR(SR_c_insr), .C_outSR(1'b0), .out_4(SR_out_4));
  SHL SL (.in_2(B), .c_inSL(1'b0), .C_outSL(SL_c_outsl), .out_3(SL_out_3));
  assign not_1_out = ~B;  // NOT_Gate not_1, 8 bits wide
  assign and_1_out = A & B;  // AND_Gate and_1, 8 bits wide
  assign or_1_out = A | B;  // OR_Gate or_1, 8 bits wide
  assign xor_1_out = A ^ B;  // XOR_Gate xor_1, 8 bits wide
  Comparator comparator_1 (.a(B), .b(A), .gt(a_larger), .eq(equal));  // open: lt
  Multiplexer #(.select(3), .width(8)) multiplexer_1 (
    .in0(somador_1_out_8b), .in1(SR_out_4), .in2(SL_out_3), .in3(not_1_out), .in4(and_1_out), .in5(or_1_out),
    .in6(xor_1_out), .in7(B), .out(U_out), .sel(in_1));
  Multiplexer #(.select(3)) multiplexer_2 (
    .in0(somador_1_c_out8b), .in1(SR_c_insr), .in2(SL_c_outsl), .in3(1'b0), .in4(1'b0), .in5(1'b0),
    .in6(1'b0), .in7(1'b0), .out(U_c_out), .sel(in_1));
  nor nor_1 (zero, U_out[0], U_out[1], U_out[2], U_out[3], U_out[4], U_out[5], U_out[6], U_out[7]);
endmodule

module clk (
  output set,
  output enable
);

  wire clock_1_out, not_1_out, t_ff_1_q;

  Clock #(.highDuration(2), .lowDuration(2)) clock_1 (.out(clock_1_out));
  not not_1 (not_1_out, clock_1_out);
  T_Flip_Flop t_ff_1 (.clk(clock_1_out), .T(1'b1), .Q(t_ff_1_q));  // open: Qn, preset, reset
  and and_1 (set, not_1_out, t_ff_1_q);
  or or_1 (enable, t_ff_1_q, clock_1_out);
endmodule

module stepper (
  output init,
  output s1,
  output s2,
  output s3,
  output s4,
  output s5,
  output s6
);

  wire clk_1_enable, decoder_1_out7;
  wire [2:0] counter_1_q;

  clk clk_1 (.enable(clk_1_enable));  // open: set
  Counter #(.max('h7), .width(3)) counter_1 (
    .D(3'b001), .Q(counter_1_q), .clk(clk_1_enable), .clr(decoder_1_out7));  // open: load, count, carry, up
  Decoder #(.select(3)) decoder_1 (
    .out0(init), .out1(s1), .out2(s2), .out3(s3), .out4(s4), .out5(s5), .out6(s6), .out7(decoder_1_out7),
    .sel(counter_1_q));  // open: en
endmodule

module bus1 (
  input  [7:0] in_1,
  input  in_2,
  output [7:0] out_3
);

  Multiplexer #(.width(8)) multiplexer_1 (.in0(in_1), .in1(8'h1), .out(out_3), .sel(in_2));
endmodule

module uc (
  input  c_out,
  input  alarg,
  input  equal,
  input  zero,
  input  [7:0] in_5,
  output bus1,
  output tmp,
  output r0s,
  output r0e,
  output r1s,
  output r1e,
  output r2s,
  output r2e,
  output r3s,
  output r3e,
  output mars,
  output [2:0] ULAop,
  output we,
  output oe,
  output led,
  output flags,
  output accs,
  output acce,
  output iars,
  output iare,
  output irs,
  output I_O,
  output D_A,
  output IO_e,
  output IO_s
);

  wire a_out, and_5_out, and_6_out, and_7_out, and_8_out, and_9_out, and_10_out, and_11_out, and_12_out,
       and_16_out, and_17_out, and_18_out, and_19_out, and_20_out, and_21_out, and_22_out, and_23_out,
       and_24_out, and_25_out, and_26_out, and_27_out, and_28_out, and_29_out, and_30_out, and_31_out,
       and_32_out, and_33_out, and_34_out, and_35_out, and_36_out, and_37_out, and_38_out, and_39_out,
       and_40_out, and_41_out, and_42_out, and_43_out, c_out_2, clk_1_enable, clk_1_set, decoder_1_out0,
       decoder_1_out1, decoder_1_out2, decoder_1_out3, decoder_2_out0, decoder_2_out1, decoder_2_out2,
       decoder_2_out3, decoder_3_out0, decoder_3_out1, decoder_3_out2, decoder_3_out3, decoder_3_out4,
       decoder_3_out5, decoder_3_out6, decoder_3_out7, decoder_4_out0, decoder_4_out1, decoder_4_out2,
       decoder_4_out3, e_out, not_1_out, not_2_out, not_3_out, or_6_out, or_7_out, or_8_out, or_9_out,
       or_10_out, or_11_out, or_12_out, or_13_out, or_14_out, or_15_out, or_16_out, stepper_1_s1,
       stepper_1_s2, stepper_1_s3, stepper_1_s4, stepper_1_s5, stepper_1_s6, z_out;

  clk clk_1 (.set(clk_1_set), .enable(clk_1_enable));
  and and_1 (iare, clk_1_enable, or_6_out);
  and and_2 (oe, clk_1_enable, or_7_out);
  and and_3 (acce, clk_1_enable, or_8_out);
  or or_1 (r0e, and_5_out, and_9_out);
  or or_2 (r1e, and_6_out, and_10_out);
  or or_3 (r2e, and_7_out, and_11_out);
  or or_4 (r3e, and_8_out, and_12_out);
  and and_4 (IO_e, clk_1_enable, and_40_out);
  and and_5 (and_5_out, clk_1_enable, or_9_out, decoder_1_out0);
  and and_6 (and_6_out, clk_1_enable, or_9_out, decoder_1_out1);
  and and_7 (and_7_out, clk_1_enable, or_9_out, decoder_1_out2);
  and and_8 (and_8_out, clk_1_enable, or_9_out, decoder_1_out3);
  and and_9 (and_9_out, clk_1_enable, or_10_out, decoder_2_out0);
  and and_10 (and_10_out, clk_1_enable, or_10_out, decoder_2_out1);
  and and_11 (and_11_out, clk_1_enable, or_10_out, decoder_2_out2);
  and and_12 (and_12_out, clk_1_enable, or_10_out, decoder_2_out3);
  or or_5 (bus1, stepper_1_s1, and_31_out, and_30_out, and_27_out);
  or or_6 (or_6_out, stepper_1_s1, and_27_out, and_29_out, and_30_out);
  or or_7 (or_7_out, stepper_1_s2, and_43_out, and_38_out, and_37_out, and_35_out);
  or or_8 (or_8_out, stepper_1_s3, and_39_out, and_42_out, and_41_out);
  or or_9 (or_9_out, and_24_out, and_36_out, and_28_out, and_32_out);
  or or_10 (or_10_out, and_26_out, and_25_out, and_34_out);
  Decoder #(.enable("false"), .select(2)) decoder_1 (
    .out0(decoder_1_out0), .out1(decoder_1_out1), .out2(decoder_1_out2), .out3(decoder_1_out3),
    .sel(in_5[1:0]));
  Decoder #(.enable("false"), .select(2)) decoder_2 (
    .out0(decoder_2_out0), .out1(decoder_2_out1), .out2(decoder_2_out2), .out3(decoder_2_out3),
    .sel(in_5[3:2]));
  and and_13 (ULAop[0], stepper_1_s5, in_5[7], in_5[4]);
  and and_14 (ULAop[1], stepper_1_s5, in_5[7], in_5[5]);
  and and_15 (ULAop[2], stepper_1_s5, in_5[7], in_5[6]);
  not not_1 (not_1_out, in_5[7]);
  Decoder #(.enable("false"), .select(3)) decoder_3 (
    .out0(decoder_3_out0), .out1(decoder_3_out1), .out2(decoder_3_out2), .out3(decoder_3_out3),
    .out4(decoder_3_out4), .out5(decoder_3_out5), .out6(decoder_3_out6), .out7(decoder_3_out7),
    .sel(in_5[6:4]));
  and and_16 (and_16_out, not_1_out, decoder_3_out0);
  and and_17 (and_17_out, not_1_out, decoder_3_out1);
  and and_18 (and_18_out, not_1_out, decoder_3_out2);
  and and_19 (and_19_out, not_1_out, decoder_3_out3);
  and and_20 (and_20_out, not_1_out, decoder_3_out4);
  and and_21 (and_21_out, not_1_out, decoder_3_out5);
  and and_22 (and_22_out, not_1_out, decoder_3_out6);
  and and_23 (and_23_out, not_1_out, decoder_3_out7);
  stepper stepper_1 (
    .init(led), .s1(stepper_1_s1), .s2(stepper_1_s2), .s3(stepper_1_s3), .s4(stepper_1_s4),
    .s5(stepper_1_s5), .s6(stepper_1_s6));
  and and_24 (and_24_out, stepper_1_s4, in_5[7]);
  and and_25 (and_25_out, stepper_1_s4, and_16_out);
  and and_26 (and_26_out, stepper_1_s4, and_17_out);
  and and_27 (and_27_out, stepper_1_s4, and_18_out);
  and and_28 (and_28_out, stepper_1_s4, and_19_out);
  and and_29 (and_29_out, stepper_1_s4, and_20_out);
  and and_30 (and_30_out, stepper_1_s4, and_21_out);
  and and_31 (and_31_out, stepper_1_s4, and_22_out);
  and and_32 (and_32_out, stepper_1_s4, and_23_out, in_5[3]);
  not not_2 (not_2_out, in_5[3]);
  and c (c_out_2, in_5[3], c_out);
  and a (a_out, in_5[2], alarg);
  and e (e_out, in_5[1], equal);
  and z (z_out, in_5[0], zero);
  and and_33 (and_33_out, in_5[4], in_5[5], in_5[6]);
  and and_34 (and_34_out, stepper_1_s5, in_5[7]);
  and and_35 (and_35_out, stepper_1_s5, and_16_out);
  and and_36 (and_36_out, stepper_1_s5, and_17_out);
  and and_37 (and_37_out, stepper_1_s5, and_18_out);
  and and_38 (and_38_out, stepper_1_s5, and_20_out);
  and and_39 (and_39_out, stepper_1_s5, and_21_out);
  and and_40 (and_40_out, stepper_1_s5, and_23_out, not_2_out);
  or or_11 (or_11_out, c_out_2, a_out, e_out, z_out);
  not not_3 (not_3_out, and_33_out);
  and and_41 (and_41_out, stepper_1_s6, in_5[7], not_3_out);
  and and_42 (and_42_out, stepper_1_s6, and_18_out);
  and and_43 (and_43_out, stepper_1_s6, and_21_out, or_11_out);
  or or_12 (or_12_out, stepper_1_s1, and_27_out, and_30_out, and_25_out, and_26_out, and_29_out);
  or or_13 (or_13_out, stepper_1_s3, and_28_out, and_38_out, and_39_out, and_42_out, and_43_out);
  or or_14 (or_14_out, stepper_1_s1, and_27_out, and_30_out, and_34_out);
  or or_15 (or_15_out, and_31_out, and_34_out);
  or or_16 (or_16_out, and_35_out, and_41_out, and_37_out, and_40_out);
  Decoder #(.enable("false"), .select(2)) decoder_4 (
    .out0(decoder_4_out0), .out1(decoder_4_out1), .out2(decoder_4_out2), .out3(decoder_4_out3),
    .sel(in_5[1:0]));
  and and_44 (irs, clk_1_set, stepper_1_s2);
  and and_45 (mars, clk_1_set, or_12_out);
  and and_46 (iars, clk_1_set, or_13_out);
  and and_47 (accs, clk_1_set, or_14_out);
  and and_48 (we, clk_1_set, and_36_out);
  and and_49 (tmp, clk_1_set, and_24_out);
  and and_50 (flags, clk_1_set, or_15_out);
  and and_51 (IO_s, clk_1_set, and_32_out);
  and and_52 (r0s, clk_1_set, or_16_out, decoder_4_out0);
  and and_53 (r1s, clk_1_set, or_16_out, decoder_4_out1);
  and and_54 (r2s, clk_1_set, or_16_out, decoder_4_out2);
  and and_55 (r3s, clk_1_set, or_16_out, decoder_4_out3);

  assign D_A = in_5[2];
  assign I_O = in_5[3];

  // Other names for the same wires on the sheet: I_Oe = IO_e; I_Os = IO_s; irQ[7:0] = in_5; ULA[2:0] = ULAop

  // Notes on the sheet:
  //   1
  //   2
  //   3
  //   4
  //   caez
  //   5
  //   6
  //   7
endmodule

module flags (
  input  in_1,
  input  in_2,
  input  in_3,
  input  in_4,
  input  reset,
  output co,
  output am,
  output eq,
  output zer
);

  Register #(.width(4)) register_1 (.D({in_4, in_3, in_2, in_1}), .Q({zer, eq, am, co}), .clk(reset));  // open: en, clr
endmodule

module monitor (
  input  [7:0] in_1,
  input  ios,
  input  da,
  input  io,
  output [6:0] out_5,
  output out_6,
  output out_7
);

  wire and_1_out, comparator_1_eq;

  Comparator comparator_1 (.a(in_1), .b(8'h1), .eq(comparator_1_eq));  // open: gt, lt
  Register #(.width(1)) register_1 (.D(comparator_1_eq), .Q(out_7), .clk(and_1_out));  // open: en, clr
  and and_1 (and_1_out, ios, da, io);
  Bit_Extender #(.out_width(7), .\type ("zero")) bit_extender_1 (.in(in_1), .out(out_5));

  assign out_6 = ios;
endmodule

module teclado (
  input  ioe,
  input  [7:0] ebarr,
  input  [6:0] etec,
  input  ios,
  input  da,
  input  io,
  output [7:0] stec,
  output out_8,
  output out_9
);

  wire and_1_out, comparator_1_eq;
  wire [7:0] bit_extender_1_out;

  T_Flip_Flop t_ff_1 (.clk(ioe), .T(1'b1), .Qn(out_8));  // open: Q, preset, reset
  Comparator comparator_1 (.a(ebarr), .b({8{1'b0}}), .eq(comparator_1_eq));  // open: gt, lt
  and and_1 (and_1_out, ios, da, io);
  Register #(.width(1)) register_1 (.D(comparator_1_eq), .Q(out_9), .clk(and_1_out));  // open: en, clr
  assign stec = ioe ? bit_extender_1_out : 8'bz;  // Controlled_Buffer controlled_buffer_1
  assign bit_extender_1_out = {{1{1'b0}}, etec};  // Bit_Extender bit_extender_1
endmodule
